// Logisim project CPU.circ as structural Verilog
module main (
  input  [31:0] A,
  input  [3:0] in_2,
  input  [31:0] B,
  output [31:0] out_4,
  output [31:0] out_5
);

  ALU alu_1 (.A(A), .B(B), .out_6(out_5), .Input(in_2), .out_7(out_4));  // open: out_4, out_5
endmodule

module ALU (
  input  [31:0] A,
  input  [31:0] B,
  input  [3:0] Input,
  output out_4,
  output out_5,
  output [31:0] out_6,
  output [31:0] out_7
);

  wire [31:0] adder_1_out, and_1_out, divider_1_out, divider_1_rem, divider_2_out, mult_signed_1_out_3,
       mult_signed_1_out_4, multiplier_1_cout, multiplier_1_out, or_1_out, subtractor_1_out, xor_1_out;

  Adder #(.width(32)) adder_1 (.a(A), .b(B), .out(adder_1_out), .cout(out_4));  // open: cin
  Subtractor #(.width(32)) subtractor_1 (.a(A), .b(B), .out(subtractor_1_out), .bout(out_5));  // open: bin
  Multiplier #(.width(32)) multiplier_1 (.a(A), .b(B), .out(multiplier_1_out), .cout(multiplier_1_cout));  // open: cin
  Divider #(.width(32)) divider_1 (.a(A), .b(B), .out(divider_1_out), .rem(divider_1_rem));  // open: upper
  mult_signed mult_signed_1 (.A(A), .B(B), .out_3(mult_signed_1_out_3), .out_4(mult_signed_1_out_4));
  Divider #(.width(32)) divider_2 (.a(A), .b(B), .out(divider_2_out));  // open: upper, rem
  assign and_1_out = A & B;  // AND_Gate and_1, 32 bits wide
  assign or_1_out = A | B;  // OR_Gate or_1, 32 bits wide
  assign xor_1_out = A ^ B;  // XOR_Gate xor_1, 32 bits wide
  Multiplexer #(.select(4), .width(32), .enable("false")) multiplexer_1 (
    .in0({32{1'b0}}), .in1({32{1'b0}}), .in2(multiplier_1_cout), .in3(divider_1_rem),
    .in4(mult_signed_1_out_4), .in5({32{1'b0}}), .in6({32{1'b0}}), .in7({32{1'b0}}), .in8({32{1'b0}}),
    .in9({32{1'b0}}), .in10({32{1'b0}}), .in11({32{1'b0}}), .in12({32{1'b0}}), .in13({32{1'b0}}),
    .in14({32{1'b0}}), .in15({32{1'b0}}), .out(out_7), .sel(Input));
  Multiplexer #(.select(4), .width(32), .enable("false")) multiplexer_2 (
    .in0(adder_1_out), .in1(subtractor_1_out), .in2(multiplier_1_out), .in3(divider_1_out),
    .in4(mult_signed_1_out_3), .in7(and_1_out), .in8(or_1_out), .in9(xor_1_out), .out(out_6), .sel(Input));  // open: in5, in6, in10, in11, in12, in13, in14, in15
endmodule

module RegisterFile (
  input  in_1,
  input  [4:0] in_2,
  input  [4:0] in_3,
  input  [4:0] in_4,
  input  [31:0] in_5,
  input  in_6,
  output [31:0] A,
  output [31:0] B
);

  wire L1, L2, L3, L4, L5, L6, L7, L8, L9, L10, L11, L12, L13, L14, L15, L16, L17, L18, L19, L20, L21, L22,
       L23, L24, L25, L26, L27, L28, L29, L30, L31, L32, R;
  wire [31:0] Q0, Q1, Q2, Q3, Q4, Q5, Q6, Q7, Q8, Q9, Q10, Q11, Q12, Q13, Q14, Q15, Q16, Q17, Q18, Q19, Q20,
       Q21, Q22, Q23, Q24, Q25, Q26, Q27, Q28, Q29, Q30, Q31;

  Demultiplexer #(.select(5), .enable("false")) demultiplexer_1 (
    .out0(L1), .out1(L2), .out2(L3), .out3(L4), .out4(L5), .out5(L6), .out6(L7), .out7(L8), .out8(L9),
    .out9(L10), .out10(L11), .out11(L12), .out12(L13), .out13(L14), .out14(L15), .out15(L16), .out16(L17),
    .out17(L18), .out18(L19), .out19(L20), .out20(L21), .out21(L22), .out22(L23), .out23(L24), .out24(L25),
    .out25(L26), .out26(L27), .out27(L28), .out28(L29), .out29(L30), .out30(L31), .out31(L32), .in(in_6),
    .sel(in_4));
  Register #(.width(32)) register_1 (.D(in_5), .en(L1), .Q(Q0), .clk(R));  // open: clr
  Register #(.width(32)) register_2 (.D(in_5), .en(L2), .Q(Q1), .clk(R));  // open: clr
  Register #(.width(32)) register_3 (.D(in_5), .en(L3), .Q(Q2), .clk(R));  // open: clr
  Register #(.width(32)) register_4 (.D(in_5), .en(L4), .Q(Q3), .clk(R));  // open: clr
  Register #(.width(32)) register_5 (.D(in_5), .en(L5), .Q(Q4), .clk(R));  // open: clr
  Register #(.width(32)) register_6 (.D(in_5), .en(L6), .Q(Q5), .clk(R));  // open: clr
  Register #(.width(32)) register_7 (.D(in_5), .en(L7), .Q(Q6), .clk(R));  // open: clr
  Register #(.width(32)) register_8 (.D(in_5), .en(L8), .Q(Q7), .clk(R));  // open: clr
  Register #(.width(32)) register_9 (.D(in_5), .en(L9), .Q(Q8), .clk(R));  // open: clr
  Register #(.width(32)) register_10 (.D(in_5), .en(L10), .Q(Q9), .clk(R));  // open: clr
  Register #(.width(32)) register_11 (.D(in_5), .en(L11), .Q(Q10), .clk(R));  // open: clr
  Register #(.width(32)) register_12 (.D(in_5), .en(L12), .Q(Q11), .clk(R));  // open: clr
  Register #(.width(32)) register_13 (.D(in_5), .en(L13), .Q(Q12), .clk(R));  // open: clr
  Register #(.width(32)) register_14 (.D(in_5), .en(L14), .Q(Q13), .clk(R));  // open: clr
  Register #(.width(32)) register_15 (.D(in_5), .en(L15), .Q(Q14), .clk(R));  // open: clr
  Register #(.width(32)) register_16 (.D(in_5), .en(L16), .Q(Q15), .clk(R));  // open: clr
  Register #(.width(32)) register_17 (.D(in_5), .en(L17), .Q(Q16), .clk(R));  // open: clr
  Register #(.width(32)) register_18 (.D(in_5), .en(L18), .Q(Q17), .clk(R));  // open: clr
  Register #(.width(32)) register_19 (.D(in_5), .en(L19), .Q(Q18), .clk(R));  // open: clr
  Register #(.width(32)) register_20 (.D(in_5), .en(L20), .Q(Q19), .clk(R));  // open: clr
  Register #(.width(32)) register_21 (.D(in_5), .en(L21), .Q(Q20), .clk(R));  // open: clr
  Register #(.width(32)) register_22 (.D(in_5), .en(L22), .Q(Q21), .clk(R));  // open: clr
  Register #(.width(32)) register_23 (.D(in_5), .en(L23), .Q(Q22), .clk(R));  // open: clr
  Register #(.width(32)) register_24 (.D(in_5), .en(L24), .Q(Q23), .clk(R));  // open: clr
  Register #(.width(32)) register_25 (.D(in_5), .en(L25), .Q(Q24), .clk(R));  // open: clr
  Register #(.width(32)) register_26 (.D(in_5), .en(L26), .Q(Q25), .clk(R));  // open: clr
  Register #(.width(32)) register_27 (.D(in_5), .en(L27), .Q(Q26), .clk(R));  // open: clr
  Register #(.width(32)) register_28 (.D(in_5), .en(L28), .Q(Q27), .clk(R));  // open: clr
  Register #(.width(32)) register_29 (.D(in_5), .en(L29), .Q(Q28), .clk(R));  // open: clr
  Register #(.width(32)) register_30 (.D(in_5), .en(L30), .Q(Q29), .clk(R));  // open: clr
  Register #(.width(32)) register_31 (.D(in_5), .en(L31), .Q(Q30), .clk(R));  // open: clr
  Register #(.width(32)) register_32 (.D(in_5), .en(L32), .Q(Q31), .clk(R));  // open: clr
  Multiplexer #(.select(5), .width(32), .enable("false")) multiplexer_1 (
    .in0(Q0), .in1(Q1), .in2(Q2), .in3(Q3), .in4(Q4), .in5(Q5), .in6(Q6), .in7(Q7), .in8(Q8), .in9(Q9),
    .in10(Q10), .in11(Q11), .in12(Q12), .in13(Q13), .in14(Q14), .in15(Q15), .in16(Q16), .in17(Q17),
    .in18(Q18), .in19(Q19), .in20(Q20), .in21(Q21), .in22(Q22), .in23(Q23), .in24(Q24), .in25(Q25),
    .in26(Q26), .in27(Q27), .in28(Q28), .in29(Q29), .in30(Q30), .in31(Q31), .out(A), .sel(in_2));
  Multiplexer #(.select(5), .width(32), .enable("false")) multiplexer_2 (
    .in0(Q0), .in1(Q1), .in2(Q2), .in3(Q3), .in4(Q4), .in5(Q5), .in6(Q6), .in7(Q7), .in8(Q8), .in9(Q9),
    .in10(Q10), .in11(Q11), .in12(Q12), .in13(Q13), .in14(Q14), .in15(Q15), .in16(Q16), .in17(Q17),
    .in18(Q18), .in19(Q19), .in20(Q20), .in21(Q21), .in22(Q22), .in23(Q23), .in24(Q24), .in25(Q25),
    .in26(Q26), .in27(Q27), .in28(Q28), .in29(Q29), .in30(Q30), .in31(Q31), .out(B), .sel(in_3));

  // Other names for the same wires on the sheet: Data[31:0] = in_5; null_write = in_6; Reloj = in_1;
  //   Selector_1[4:0] = in_2; Selector_2[4:0] = in_3; Selector_3[4:0] = in_4
endmodule

module mult_signed (
  input  [31:0] A,
  input  [31:0] B,
  output [31:0] out_3,
  output [31:0] out_4
);

  wire overflow, xor_1_out, xor_2_out;
  wire [31:0] adder_1_out, adder_2_out, adder_3_out, adder_4_out, multiplexer_1_out, multiplexer_2_out,
       multiplier_1_cout, multiplier_1_out, negator_1_out, negator_2_out, negator_3_out, negator_4_out;

  Negator #(.width(32)) negator_1 (.in(A), .out(negator_1_out));
  Negator #(.width(32)) negator_2 (.in(B), .out(negator_2_out));
  Adder #(.width(32)) adder_1 (.a(negator_1_out), .b(32'h1), .out(adder_1_out));  // open: cin, cout
  Adder #(.width(32)) adder_2 (.a(negator_2_out), .b(32'h1), .out(adder_2_out));  // open: cin, cout
  Multiplexer #(.width(32), .enable("false")) multiplexer_1 (
    .in0(A), .in1(adder_1_out), .out(multiplexer_1_out), .sel(A[0]));
  Multiplexer #(.width(32), .enable("false")) multiplexer_2 (
    .in0(B), .in1(adder_2_out), .out(multiplexer_2_out), .sel(B[0]));
  Multiplier #(.width(32)) multiplier_1 (
    .a(multiplexer_1_out), .b(multiplexer_2_out), .out(multiplier_1_out), .cout(multiplier_1_cout));  // open: cin
  Negator #(.width(32)) negator_3 (.in(multiplier_1_out), .out(negator_3_out));
  Negator #(.width(32)) negator_4 (.in(multiplier_1_cout), .out(negator_4_out));
  Adder #(.width(32)) adder_3 (.a(negator_3_out), .b(32'h1), .out(adder_3_out), .cout(overflow));  // open: cin
  Adder #(.width(32)) adder_4 (.a(negator_4_out), .b({{31{1'b0}}, overflow}), .out(adder_4_out));  // open: cin, cout
  Multiplexer #(.width(32), .enable("false")) multiplexer_3 (
    .in0(multiplier_1_out), .in1(adder_3_out), .out(out_3), .sel(xor_1_out));
  xor xor_1 (xor_1_out, A[0], B[0]);
  Multiplexer #(.width(32), .enable("false")) multiplexer_4 (
    .in0(multiplier_1_cout), .in1(adder_4_out), .out(out_4), .sel(xor_2_out));
  xor xor_2 (xor_2_out, A[0], B[0]);

  // Other names for the same wires on the sheet: Signo = A[0]; Signo2 = B[0]
endmodule

module InstructionDecoder (
  input  [31:0] in_1,
  output out_2,
  output out_3,
  output out_4,
  output out_5,
  output out_6,
  output [4:0] out_7,
  output out_8,
  output out_9,
  output out_10,
  output out_11,
  output out_12,
  output [4:0] out_13,
  output out_14,
  output out_15,
  output out_16,
  output out_17,
  output out_18,
  output [4:0] out_19,
  output out_20,
  output out_21,
  output out_22,
  output out_23,
  output out_24,
  output out_25,
  output out_26,
  output out_27,
  output out_28,
  output out_29,
  output out_30,
  output out_31,
  output out_32,
  output [25:0] out_33,
  output out_34,
  output out_35,
  output out_36,
  output out_37,
  output out_38,
  output out_39,
  output out_40,
  output out_41,
  output [15:0] out_42
);

  wire _000000, _111111, comparator_2_eq, comparator_3_eq, comparator_4_eq, comparator_5_eq, comparator_6_eq,
       comparator_7_eq, comparator_8_eq, comparator_9_eq, comparator_10_eq, comparator_11_eq,
       comparator_12_eq, comparator_13_eq, comparator_14_eq, comparator_15_eq, comparator_16_eq,
       comparator_17_eq, comparator_19_eq, comparator_20_eq, comparator_21_eq, comparator_22_eq,
       comparator_23_eq, comparator_24_eq, comparator_25_eq, comparator_26_eq;

  Comparator #(.width(6)) comparator_1 (.a(in_1[31:26]), .b({6{1'b0}}), .eq(_000000));  // open: gt, lt
  and and_1 (out_2, _000000, comparator_2_eq);
  Comparator #(.width(6)) comparator_2 (.a(in_1[5:0]), .b({6{1'b0}}), .eq(comparator_2_eq));  // open: gt, lt
  and and_2 (out_8, _000000, comparator_3_eq);
  Comparator #(.width(6)) comparator_3 (.a(in_1[5:0]), .b(6'b100000), .eq(comparator_3_eq));  // open: gt, lt
  and and_3 (out_14, _000000, comparator_4_eq);
  Comparator #(.width(6)) comparator_4 (.a(in_1[5:0]), .b(6'b100010), .eq(comparator_4_eq));  // open: gt, lt
  and and_4 (out_20, _000000, comparator_5_eq);
  Comparator #(.width(6)) comparator_5 (.a(in_1[5:0]), .b(6'b011000), .eq(comparator_5_eq));  // open: gt, lt
  and and_5 (out_25, _000000, comparator_6_eq);
  Comparator #(.width(6)) comparator_6 (.a(in_1[5:0]), .b(6'b011001), .eq(comparator_6_eq));  // open: gt, lt
  and and_6 (out_29, _000000, comparator_7_eq);
  Comparator #(.width(6)) comparator_7 (.a(in_1[5:0]), .b(6'b011010), .eq(comparator_7_eq));  // open: gt, lt
  and and_7 (out_34, _000000, comparator_8_eq);
  Comparator #(.width(6)) comparator_8 (.a(in_1[5:0]), .b(6'b011011), .eq(comparator_8_eq));  // open: gt, lt
  and and_8 (out_38, _000000, comparator_9_eq);
  Comparator #(.width(6)) comparator_9 (.a(in_1[5:0]), .b(6'b101010), .eq(comparator_9_eq));  // open: gt, lt
  and and_9 (out_3, _000000, comparator_10_eq);
  Comparator #(.width(6)) comparator_10 (.a(in_1[5:0]), .b(6'b101011), .eq(comparator_10_eq));  // open: gt, lt
  and and_10 (out_9, _000000, comparator_11_eq);
  Comparator #(.width(6)) comparator_11 (.a(in_1[5:0]), .b(6'b100100), .eq(comparator_11_eq));  // open: gt, lt
  and and_11 (out_15, _000000, comparator_12_eq);
  Comparator #(.width(6)) comparator_12 (.a(in_1[5:0]), .b(6'b100101), .eq(comparator_12_eq));  // open: gt, lt
  and and_12 (out_21, _000000, comparator_13_eq);
  Comparator #(.width(6)) comparator_13 (.a(in_1[5:0]), .b(6'b100111), .eq(comparator_13_eq));  // open: gt, lt
  and and_13 (out_26, _000000, comparator_14_eq);
  Comparator #(.width(6)) comparator_14 (.a(in_1[5:0]), .b(6'b101000), .eq(comparator_14_eq));  // open: gt, lt
  and and_14 (out_30, _000000, comparator_15_eq);
  Comparator #(.width(6)) comparator_15 (.a(in_1[5:0]), .b(6'b001000), .eq(comparator_15_eq));  // open: gt, lt
  and and_15 (out_35, _000000, comparator_16_eq);
  Comparator #(.width(6)) comparator_16 (.a(in_1[5:0]), .b(6'b010000), .eq(comparator_16_eq));  // open: gt, lt
  and and_16 (out_39, _000000, comparator_17_eq);
  Comparator #(.width(6)) comparator_17 (.a(in_1[5:0]), .b(6'b010010), .eq(comparator_17_eq));  // open: gt, lt
  Comparator #(.width(6)) comparator_18 (.a(in_1[31:26]), .b({6{1'b1}}), .eq(_111111));  // open: gt, lt
  Comparator #(.width(6)) comparator_19 (.a(in_1[5:0]), .b({6{1'b1}}), .eq(comparator_19_eq));  // open: gt, lt
  Comparator #(.width(6)) comparator_20 (.a(in_1[5:0]), .b(6'b000001), .eq(comparator_20_eq));  // open: gt, lt
  Comparator #(.width(6)) comparator_21 (.a(in_1[5:0]), .b(6'b000010), .eq(comparator_21_eq));  // open: gt, lt
  Comparator #(.width(6)) comparator_22 (.a(in_1[5:0]), .b(6'b000100), .eq(comparator_22_eq));  // open: gt, lt
  and and_17 (out_12, _111111, comparator_19_eq);
  and and_18 (out_18, _111111, comparator_20_eq);
  and and_19 (out_24, _111111, comparator_21_eq);
  and and_20 (out_6, _111111, comparator_22_eq);
  Comparator #(.width(6)) comparator_23 (.a(in_1[31:26]), .b(6'b111000), .eq(comparator_23_eq));  // open: gt, lt
  Comparator #(.width(6)) comparator_24 (.a(in_1[5:0]), .b({6{1'b0}}), .eq(comparator_24_eq));  // open: gt, lt
  Comparator #(.width(6)) comparator_25 (.a(in_1[31:26]), .b(6'b111000), .eq(comparator_25_eq));  // open: gt, lt
  Comparator #(.width(6)) comparator_26 (.a(in_1[5:0]), .b(6'b000001), .eq(comparator_26_eq));  // open: gt, lt
  and and_21 (out_37, comparator_23_eq, comparator_24_eq);
  and and_22 (out_41, comparator_25_eq, comparator_26_eq);
  Comparator #(.width(6)) comparator_27 (.a(in_1[31:26]), .b(6'b100011), .eq(out_4));  // open: gt, lt
  Comparator #(.width(6)) comparator_28 (.a(in_1[31:26]), .b(6'b001000), .eq(out_5));  // open: gt, lt
  Comparator #(.width(6)) comparator_29 (.a(in_1[31:26]), .b(6'b001010), .eq(out_11));  // open: gt, lt
  Comparator #(.width(6)) comparator_30 (.a(in_1[31:26]), .b(6'b001011), .eq(out_17));  // open: gt, lt
  Comparator #(.width(6)) comparator_31 (.a(in_1[31:26]), .b(6'b001100), .eq(out_23));  // open: gt, lt
  Comparator #(.width(6)) comparator_32 (.a(in_1[31:26]), .b(6'b001101), .eq(out_28));  // open: gt, lt
  Comparator #(.width(6)) comparator_33 (.a(in_1[31:26]), .b(6'b001110), .eq(out_32));  // open: gt, lt
  Comparator #(.width(6)) comparator_34 (.a(in_1[31:26]), .b(6'b101011), .eq(out_10));  // open: gt, lt
  Comparator #(.width(6)) comparator_35 (.a(in_1[31:26]), .b(6'b000100), .eq(out_16));  // open: gt, lt
  Comparator #(.width(6)) comparator_36 (.a(in_1[31:26]), .b(6'b000101), .eq(out_22));  // open: gt, lt
  Comparator #(.width(6)) comparator_37 (.a(in_1[31:26]), .b(6'b000110), .eq(out_27));  // open: gt, lt
  Comparator #(.width(6)) comparator_38 (.a(in_1[31:26]), .b(6'b000111), .eq(out_31));  // open: gt, lt
  Comparator #(.width(6)) comparator_39 (.a(in_1[31:26]), .b(6'b000001), .eq(out_36));  // open: gt, lt
  Comparator #(.width(6)) comparator_40 (.a(in_1[31:26]), .b(6'b000010), .eq(out_40));  // open: gt, lt

  assign out_7 = in_1[25:21];
  assign out_13 = in_1[20:16];
  assign out_19 = in_1[15:11];
  assign out_33 = in_1[25:0];
  assign out_42 = in_1[15:0];

  // Other names for the same wires on the sheet: Add = out_8; Addi = out_5; And = out_9; Andi = out_23; Bgtz = out_31;
  //   Blez = out_27; Bltz = out_36; Bne = out_22; Bqe = out_16; Const[15:0] = in_1[15:0]; Dest[25:0] = in_1[25:0];
  //   FC[5:0] = in_1[5:0]; RD[4:0] = in_1[15:11]; RT[4:0] = in_1[20:16]; RS[4:0] = in_1[25:21]; Div = out_29;
  //   Divu = out_34; Halt = out_12; J = out_40; Jr = out_30; Kbd = out_6; Lw = out_4; Mfhi = out_35; Mflo = out_39;
  //   Mult = out_20; Mulu = out_25; Nop = out_2; Nor = out_21; OP[5:0] = in_1[31:26]; Or = out_15; Ori = out_28;
  //   Pop = out_37; Push = out_41; Rnd = out_24; Slt = out_38; Slti = out_11; Sltiu = out_17; Sltu = out_3;
  //   Sub = out_14; Sw = out_10; Tty = out_18; Xor = out_26; Xori = out_32
endmodule

module Data_Path (
  input  [31:0] in_1,
  output [31:0] Output
);

  wire R;
  wire [0:0] operation;
  wire [4:0] instructiondecoder_1_out_7, instructiondecoder_1_out_13, instructiondecoder_1_out_19;
  wire [31:0] Program_Counter_q, registerfile_1_a, registerfile_1_b;

  Register #(.width(32)) Program_Counter (.D(in_1), .Q(Program_Counter_q), .clk(R));  // open: en, clr
  InstructionDecoder instructiondecoder_1 (
    .out_7(instructiondecoder_1_out_7), .in_1(Program_Counter_q), .out_8(operation[0]),
    .out_13(instructiondecoder_1_out_13), .out_19(instructiondecoder_1_out_19));  // open: out_2, out_3, out_4, out_5, out_9, out_10, out_11, out_33, out_14, out_15, out_16, out_17, out_20, out_21, out_22, out_23, out_42, out_25, out_26, out_27, out_28, out_29, out_30, out_31, out_32, out_12, out_6, out_34, out_35, out_36, out_37, out_18, out_38, out_39, out_40, out_41, out_24
  Clock clock_1 (.out(R));
  RegisterFile registerfile_1 (
    .in_2(instructiondecoder_1_out_7), .in_3(instructiondecoder_1_out_13),
    .in_4(instructiondecoder_1_out_19), .in_5(Output), .A(registerfile_1_a), .B(registerfile_1_b), .in_1(R),
    .in_6(1'b1));
  ALU alu_1 (
    .A(registerfile_1_a), .B(registerfile_1_b), .out_6(Output), .Input({3'b000, operation[0]}));  // open: out_4, out_5, out_7
endmodule
