// Logisim project s-mips.circ as structural Verilog: 18 circuits, main circuit S-MIPS Board
module S_MIPS_Board (
  input  DESHABILITAR_DISPATCHER,
  output halt
);

  wire button_1_out, CLK, CS, d_ff_1_q, LCLR, LoadRAM, LoadRAMOn, LW, R_R_W, R_W, ram_dispatcher_1_finished,
       RCS, Reset_out, RST, TTY_EN;
  wire [2:0] KDB;
  wire [3:0] LMask, Mask, ram_1_read_time, ram_1_write_time, RMask;
  wire [6:0] KDB_DATA, TTY_DATA;
  wire [15:0] Addr, LAddr, RAddr;
  wire [31:0] I0, I1, I2, I3, LData, ram_1_data_out_0, ram_1_data_out_1, ram_1_data_out_2, ram_1_data_out_3,
       RI0, RI1, RI2, RI3;

  TTY #(.rows(25), .cols(80)) tty_1 (.data(TTY_DATA), .clk(CLK), .we(TTY_EN), .clr(RST));
  not not_1 (LoadRAMOn, ram_dispatcher_1_finished);
  RAM_Dispatcher ram_dispatcher_1 (
    .WriteTime(ram_1_write_time), .Clock(CLK), .Data(LData), .Address(LAddr), .Mask(LMask),
    .Finished(ram_dispatcher_1_finished), .Write(LW), .CLR(LCLR));
  Keyboard #(.buflen(64)) keyboard_1 (.clk(CLK), .re(KDB[0]), .avail(KDB[2]), .data(KDB_DATA));  // open: clr
  RAM ram_1 (
    .Address(RAddr), .Data_Out_0(ram_1_data_out_0), .Data_Out_1(ram_1_data_out_1),
    .Data_Out_2(ram_1_data_out_2), .Data_Out_3(ram_1_data_out_3), .Data_In_0(RI0), .Data_In_1(RI1),
    .Data_In_2(RI2), .Data_In_3(RI3), .Mask(RMask), .nRead_Write(R_R_W), .Chip_Select(RCS),
    .Read_Time(ram_1_read_time), .Reset(button_1_out), .Write_Time(ram_1_write_time));
  Button button_1 (.out(button_1_out));
  D_Flip_Flop d_ff_1 (.clk(CLK), .D(1'b1), .Q(d_ff_1_q), .reset(Reset_out));  // open: Qn, preset, en
  Button Reset (.out(Reset_out));
  S_MIPS s_mips_1 (
    .Kbd_Enable(KDB[0]), .Address(Addr), .Kbd_Clear(KDB[1]), .Kbd_Available(KDB[2]), .RAM_In_0(I0),
    .Kbd_ASCII_Data(KDB_DATA), .RAM_In_1(I1), .TTY_Enable(TTY_EN), .RAM_In_2(I2), .RAM_In_3(I3),
    .TTY_ASCII_Data(TTY_DATA), .Reset(RST), .RAM_Out_0(ram_1_data_out_0), .Clock(CLK),
    .RAM_Out_1(ram_1_data_out_1), .Stop(halt), .RAM_Out_2(ram_1_data_out_2), .RAM_Out_3(ram_1_data_out_3),
    .Mask(Mask), .Read_Time(ram_1_read_time), .Write_Time(ram_1_write_time), .nRead_Write(R_W),
    .Chip_Select(CS));
  D_Flip_Flop d_ff_2 (.clk(CLK), .D(d_ff_1_q), .Qn(LCLR), .reset(Reset_out));  // open: Q, preset, en
  or or_1 (RST, LCLR, LoadRAM);
  Clock clock_1 (.out(CLK));
  Multiplexer #(.width(32), .enable("false")) multiplexer_1 (.in0(I0), .in1(LData), .out(RI0), .sel(LoadRAM));
  Multiplexer #(.width(32), .enable("false")) multiplexer_2 (.in0(I1), .in1(LData), .out(RI1), .sel(LoadRAM));
  Multiplexer #(.width(32), .enable("false")) multiplexer_3 (.in0(I2), .in1(LData), .out(RI2), .sel(LoadRAM));
  Multiplexer #(.width(32), .enable("false")) multiplexer_4 (.in0(I3), .in1(LData), .out(RI3), .sel(LoadRAM));
  and and_1 (LoadRAM, ~DESHABILITAR_DISPATCHER, LoadRAMOn);  // AND_Gate
  Multiplexer #(.width(16), .enable("false")) multiplexer_5 (.in0(Addr), .in1(LAddr), .out(RAddr), .sel(LoadRAM));
  Multiplexer #(.width(4), .enable("false")) multiplexer_6 (.in0(Mask), .in1(LMask), .out(RMask), .sel(LoadRAM));
  Multiplexer #(.enable("false")) multiplexer_7 (.in0(CS), .in1(LW), .out(RCS), .sel(LoadRAM));
  Multiplexer #(.enable("false")) multiplexer_8 (.in0(R_W), .in1(LW), .out(R_R_W), .sel(LoadRAM));

  // Notes on the sheet:
  //   NO MODIFICAR
  //   Keyboard
endmodule

module RAM (
  input  [15:0] Address,
  input  [31:0] Data_In_0,
  input  [31:0] Data_In_1,
  input  [31:0] Data_In_2,
  input  [31:0] Data_In_3,
  input  [3:0] Mask,
  input  nRead_Write,
  input  Chip_Select,
  input  Reset,
  output [31:0] Data_Out_0,
  output [31:0] Data_Out_1,
  output [31:0] Data_Out_2,
  output [31:0] Data_Out_3,
  output [3:0] Read_Time,
  output [3:0] Write_Time
);

  wire and_2_out, and_3_out, and_4_out, and_5_out, and_6_out, and_7_out, and_8_out, and_9_out, Changed, CLK,
       comparator_2_eq, comparator_3_eq, comparator_4_eq, comparator_5_eq, comparator_6_eq, Count,
       demultiplexer_3_out0, Idle, Idle_q, Load, Load0, Load1, nand_1_out, or_1_out, or_2_out, or_3_out,
       or_4_out, or_5_out, or_6_out, or_7_out, or_8_out, or_9_out, or_10_out, Proc_q, Update_Mem, Zero_Time;
  wire [3:0] counter_1_q, multiplexer_1_out, subtractor_1_out;
  wire [31:0] register_1_q, register_2_q, register_3_q, register_4_q, register_5_q;

  // Probe on 4'b0011
  // Probe on 4'b0010
  Multiplexer #(.width(4), .enable("false")) multiplexer_1 (
    .in0(4'b0011), .in1(4'b0010), .out(multiplexer_1_out), .sel(nRead_Write));
  or or_1 (or_1_out, Idle, Update_Mem);
  or or_2 (or_2_out, ~Chip_Select, Reset);  // OR_Gate
  Subtractor #(.width(4)) subtractor_1 (.a(multiplexer_1_out), .b(4'b0010), .out(subtractor_1_out));  // open: bin, bout
  Demultiplexer #(.enable("false")) demultiplexer_1 (.out0(Idle), .out1(Load0), .in(Idle_q), .sel(Changed));
  D_Flip_Flop u_Idle (.clk(CLK), .D(or_1_out), .Q(Idle_q), .preset(or_2_out));  // open: Qn, en, reset
  // Probe on counter_1_q
  Counter_part #(.width(4), .max('hf)) counter_1 (
    .load(Load), .D(subtractor_1_out), .count(Count), .Q(counter_1_q), .clk(CLK), .clr(or_3_out));  // open: carry
  or or_3 (or_3_out, ~Chip_Select, Reset);  // OR_Gate
  Comparator #(.width(4), .mode("unsigned")) comparator_1 (
    .a(4'b0000), .b(counter_1_q), .eq(Zero_Time));  // open: gt, lt
  or or_4 (or_4_out, Count, Load0, Load1);
  Register #(.width(32)) register_1 (.D(Data_In_0), .en(Chip_Select), .Q(register_1_q), .clk(CLK), .clr(or_5_out));
  or or_5 (or_5_out, ~Chip_Select, Reset);  // OR_Gate
  Register #(.width(32)) register_2 (.D(Data_In_1), .en(Chip_Select), .Q(register_2_q), .clk(CLK), .clr(or_6_out));
  or or_6 (or_6_out, ~Chip_Select, Reset);  // OR_Gate
  Register #(.width(32)) register_3 (.D(Data_In_2), .en(Chip_Select), .Q(register_3_q), .clk(CLK), .clr(or_7_out));
  or or_7 (or_7_out, ~Chip_Select, Reset);  // OR_Gate
  Register #(.width(32)) register_4 (.D(Data_In_3), .en(Chip_Select), .Q(register_4_q), .clk(CLK), .clr(or_8_out));
  or or_8 (or_8_out, ~Chip_Select, Reset);  // OR_Gate
  Register #(.width(32)) register_5 (
    .D({{11{1'b1}}, nRead_Write, Mask, Address}), .en(Chip_Select), .Q(register_5_q), .clk(CLK),
    .clr(or_9_out));
  or or_9 (or_9_out, ~Chip_Select, Reset);  // OR_Gate
  D_Flip_Flop Proc (.clk(CLK), .D(or_4_out), .Q(Proc_q), .reset(or_10_out));  // open: Qn, preset, en
  or or_10 (or_10_out, ~Chip_Select, Reset);  // OR_Gate
  Demultiplexer #(.enable("false")) demultiplexer_2 (
    .out0(Count), .out1(Update_Mem), .in(demultiplexer_3_out0), .sel(Zero_Time));
  Demultiplexer #(.enable("false")) demultiplexer_3 (
    .out0(demultiplexer_3_out0), .out1(Load1), .in(Proc_q), .sel(Changed));
  Clock clock_1 (.out(CLK));
  Comparator #(.width(32)) comparator_2 (.a(register_1_q), .b(Data_In_0), .eq(comparator_2_eq));  // open: gt, lt
  Comparator #(.width(32)) comparator_3 (.a(register_2_q), .b(Data_In_1), .eq(comparator_3_eq));  // open: gt, lt
  Comparator #(.width(32)) comparator_4 (.a(register_3_q), .b(Data_In_2), .eq(comparator_4_eq));  // open: gt, lt
  Comparator #(.width(32)) comparator_5 (.a(register_4_q), .b(Data_In_3), .eq(comparator_5_eq));  // open: gt, lt
  Comparator #(.width(32)) comparator_6 (
    .a(register_5_q), .b({{11{1'b1}}, nRead_Write, Mask, Address}), .eq(comparator_6_eq));  // open: gt, lt
  nand nand_1 (nand_1_out, comparator_6_eq, comparator_2_eq, comparator_3_eq, comparator_4_eq, comparator_5_eq);
  and and_1 (Changed, nand_1_out, Chip_Select);
  or or_11 (Load, Count, Load1, Load0);
  and and_2 (and_2_out, Mask[0], Update_Mem, nRead_Write);
  and and_3 (and_3_out, Mask[1], Update_Mem, nRead_Write);
  and and_4 (and_4_out, Mask[2], Update_Mem, nRead_Write);
  and and_5 (and_5_out, Mask[3], Update_Mem, nRead_Write);
  RAM_part #(.addrWidth(16), .dataWidth(32), .bus("separate")) ram_1 (
    .addr(Address), .din(Data_In_0), .data(Data_Out_0), .str(and_2_out), .sel(Chip_Select), .clk(CLK),
    .ld(and_6_out), .clr(Reset));
  and and_6 (and_6_out, ~nRead_Write, Idle);  // AND_Gate
  RAM_part #(.addrWidth(16), .dataWidth(32), .bus("separate")) ram_2 (
    .addr(Address), .din(Data_In_1), .data(Data_Out_1), .str(and_3_out), .sel(Chip_Select), .clk(CLK),
    .ld(and_7_out), .clr(Reset));
  and and_7 (and_7_out, ~nRead_Write, Idle);  // AND_Gate
  RAM_part #(.addrWidth(16), .dataWidth(32), .bus("separate")) ram_3 (
    .addr(Address), .din(Data_In_2), .data(Data_Out_2), .str(and_4_out), .sel(Chip_Select), .clk(CLK),
    .ld(and_8_out), .clr(Reset));
  and and_8 (and_8_out, ~nRead_Write, Idle);  // AND_Gate
  RAM_part #(.addrWidth(16), .dataWidth(32), .bus("separate")) ram_4 (
    .addr(Address), .din(Data_In_3), .data(Data_Out_3), .str(and_5_out), .sel(Chip_Select), .clk(CLK),
    .ld(and_9_out), .clr(Reset));
  and and_9 (and_9_out, ~nRead_Write, Idle);  // AND_Gate

  assign Read_Time = 4'b0011;
  assign Write_Time = 4'b0010;

  // Other names for the same wires on the sheet: M0 = Mask[0]; M1 = Mask[1]; M2 = Mask[2]; M3 = Mask[3];
  //   RW = nRead_Write; CLR = Reset; CS = Chip_Select; Load2 = Count

  // Notes on the sheet:
  //   NO MODIFICAR
  //   excepto quizás los valores RT y WT
  //   BANK0
  //   BANK1
  //   BANK2
  //   BANK3
endmodule

module S_MIPS (
  input  Kbd_Available,
  input  [6:0] Kbd_ASCII_Data,
  input  [31:0] RAM_Out_0,
  input  [31:0] RAM_Out_1,
  input  Reset,
  input  [31:0] RAM_Out_2,
  input  Clock,
  input  [31:0] RAM_Out_3,
  input  [3:0] Read_Time,
  input  [3:0] Write_Time,
  output Kbd_Enable,
  output [15:0] Address,
  output Kbd_Clear,
  output TTY_Enable,
  output [6:0] TTY_ASCII_Data,
  output Stop,
  output [31:0] RAM_In_0,
  output [31:0] RAM_In_1,
  output [31:0] RAM_In_2,
  output [31:0] RAM_In_3,
  output [3:0] Mask,
  output nRead_Write,
  output Chip_Select
);

  wire control_unit_1_out_9, ENIns, EnPC, getData, getIns, ram_interaction_1_out_15,
       ram_interaction_1_out_16, ram_interaction_1_out_17, Start, TTY, write;
  wire [2:0] typeIns;
  wire [31:0] AddressDP, DataIn, le_2_output, OutPut, ram_interaction_1_ram_in_0, ram_interaction_1_ram_in_1,
       ram_interaction_1_ram_in_2, ram_interaction_1_ram_in_3;

  LE le_1 (.in_1(OutPut), .Output(RAM_In_0));
  D_Flip_Flop #(.trigger("falling")) d_ff_1 (.clk(Clock), .D(Reset), .Q(Start));  // open: Qn, preset, en, reset
  RAM_interaction ram_interaction_1 (
    .Address(Address), .in_1(AddressDP), .Mask(Mask), .Read_Time(Read_Time), .in_4(Clock),
    .Write_Time(Write_Time), .RAM_Out_0(RAM_Out_0), .RAM_Out_1(RAM_Out_1), .RAM_Out_2(RAM_Out_2),
    .nRead_Write(nRead_Write), .RAM_Out_3(RAM_Out_3), .Chip_Select(Chip_Select),
    .RAM_In_0(ram_interaction_1_ram_in_0), .RAM_In_1(ram_interaction_1_ram_in_1),
    .RAM_In_2(ram_interaction_1_ram_in_2), .RAM_In_3(ram_interaction_1_ram_in_3),
    .out_15(ram_interaction_1_out_15), .in_5(write), .in_6(getData), .out_16(ram_interaction_1_out_16),
    .in_7(getIns), .out_17(ram_interaction_1_out_17), .in_3(Reset));
  LE le_2 (.in_1(DataIn), .Output(le_2_output));
  Multiplexer #(.select(2), .width(32), .enable("false")) multiplexer_1 (
    .in0(ram_interaction_1_ram_in_0), .in1(ram_interaction_1_ram_in_1), .in2(ram_interaction_1_ram_in_2),
    .in3(ram_interaction_1_ram_in_3), .out(DataIn), .sel(AddressDP[3:2]));
  Control_Unit control_unit_1 (
    .start(Start), .in_2(Reset), .reloj(Clock), .in_4(ram_interaction_1_out_17),
    .in_5(ram_interaction_1_out_16), .in_6(ram_interaction_1_out_15), .in_7(typeIns), .in_8(TTY),
    .out_9(control_unit_1_out_9), .out_10(write), .out_11(getData), .out_12(getIns), .out_13(EnPC),
    .out_14(ENIns), .out_15(TTY_Enable), .out_16(Kbd_Enable), .out_17(Stop));
  Data_Path data_path_1 (
    .in_3(EnPC), .Data_RAM(le_2_output), .Enable(ENIns), .address(AddressDP), .in_2(Clock), .out_10(typeIns),
    .Output(OutPut), .in_1(Reset), .Tty(TTY), .Tty_2(TTY_ASCII_Data), .KBD(Kbd_ASCII_Data),
    .in_6(control_unit_1_out_9));

  assign Kbd_Clear = Reset;
  assign RAM_In_1 = RAM_In_0;
  assign RAM_In_2 = RAM_In_0;
  assign RAM_In_3 = RAM_In_0;

  // Other names for the same wires on the sheet: CLK = Clock; CLR = Reset; CS = Chip_Select;
  //   KBD_AVAIL = Kbd_Available; KBD_DATA[6:0] = Kbd_ASCII_Data; RAM_A[15:0] = Address; RAM_INPUT_0[31:0] = RAM_In_0;
  //   RAM_INPUT_1[31:0] = RAM_In_0; RAM_INPUT_2[31:0] = RAM_In_0; RAM_INPUT_3[31:0] = RAM_In_0; RAM_MASK[3:0] = Mask;
  //   RAM_OUTPUT_0[31:0] = RAM_Out_0; RAM_OUTPUT_1[31:0] = RAM_Out_1; RAM_OUTPUT_2[31:0] = RAM_Out_2;
  //   RAM_OUTPUT_3[31:0] = RAM_Out_3; RW = nRead_Write; TTY_DATA[6:0] = TTY_ASCII_Data

  // Notes on the sheet:
  //   RAM ADDRESS
  //   DATA FROM RAM
  //   DATA TO RAM
  //   DATA WRITE MASK
  //   RAM TIMING
  //   RAM CONTROL
  //   KEYBOARD
  //   TTY
  //   SEQUENCING
endmodule

module RAM_Dispatcher (
  input  [3:0] WriteTime,
  input  Clock,
  input  CLR,
  output [31:0] Data,
  output [15:0] Address,
  output [3:0] Mask,
  output Finished,
  output Write
);

  wire demultiplexer_2_out1, demultiplexer_3_out1, End, IDLE_q, IncAddr, Load, or_1_out, or_2_out, While_q,
       WriteEnd;
  wire [3:0] counter_1_q;
  wire [31:0] CurrentAddress_q;

  Counter_part #(.width(32), .max('hffffffff)) CurrentAddress (
    .count(IncAddr), .Q({CurrentAddress_q[31:18], Address, CurrentAddress_q[1:0]}), .clk(Clock), .clr(CLR));  // open: load, D, carry
  or or_1 (or_1_out, IncAddr, demultiplexer_3_out1, Finished);
  D_Flip_Flop IDLE (.clk(Clock), .D(or_1_out), .Q(IDLE_q), .preset(CLR));  // open: Qn, en, reset
  Demultiplexer #(.enable("false")) demultiplexer_1 (.out0(Load), .out1(Finished), .in(IDLE_q), .sel(End));
  D_Flip_Flop While (.clk(Clock), .D(or_2_out), .Q(While_q), .reset(CLR));  // open: Qn, preset, en
  or or_2 (or_2_out, Write, Load);
  RAM_part #(.addrWidth(18), .dataWidth(32)) ram_1 (
    .addr({Address, CurrentAddress_q[1:0]}), .data(Data), .clk(Clock));  // open: sel, ld, clr
  Demultiplexer #(.enable("false")) demultiplexer_2 (
    .out0(Write), .out1(demultiplexer_2_out1), .in(While_q), .sel(WriteEnd));
  Decoder #(.select(2)) decoder_1 (
    .out0(Mask[0]), .out1(Mask[1]), .out2(Mask[2]), .out3(Mask[3]), .sel(CurrentAddress_q[1:0]));  // open: en
  Demultiplexer #(.enable("false")) demultiplexer_3 (
    .out0(IncAddr), .out1(demultiplexer_3_out1), .in(demultiplexer_2_out1), .sel(End));
  Counter_part #(.width(4), .max('hf)) counter_1 (
    .load(Load), .D(WriteTime), .count(Write), .Q(counter_1_q), .clk(Clock));  // open: carry, clr
  Comparator #(.width(32)) comparator_1 (.a(Data), .b({32{1'b1}}), .eq(End));  // open: gt, lt
  Comparator #(.width(4)) comparator_2 (.a(4'b0000), .b(counter_1_q), .eq(WriteEnd));  // open: gt, lt

  // Other names for the same wires on the sheet: CLK = Clock; Count = Write; WT[3:0] = WriteTime
endmodule

module ALU (
  input  [31:0] A,
  input  [31:0] B,
  input  [3:0] Input,
  input  write,
  input  reset,
  input  reloj,
  output [31:0] out_7,
  output [31:0] Lo,
  output [31:0] Hi
);

  wire and_2_out, SLt1, SLtu1;
  wire [31:0] adder_1_out, and_1_out, demultiplexer_1_out1, divider_1_out, divider_1_rem, division_1_div,
       division_1_divrem, multiplexer_1_out, multiplexer_2_out, multiplicacion_1_oh, multiplicacion_1_ol,
       multiplier_1_cout, multiplier_1_out, nor_1_out, or_1_out, subtractor_1_out, xor_1_out;

  Adder #(.width(32)) adder_1 (.a(A), .b(B), .out(adder_1_out));  // open: cin, cout
  Subtractor #(.width(32)) subtractor_1 (.a(A), .b(B), .out(subtractor_1_out));  // open: bin, bout
  assign and_1_out = A & B;  // AND_Gate and_1, 32 bits wide
  assign or_1_out = A | B;  // OR_Gate or_1, 32 bits wide
  assign nor_1_out = ~(A | B);  // NOR_Gate nor_1, 32 bits wide
  assign xor_1_out = A ^ B;  // XOR_Gate xor_1, 32 bits wide
  Comparator #(.width(32)) comparator_1 (.a(A), .b(B), .lt(SLt1));  // open: gt, eq
  Comparator #(.width(32), .mode("unsigned")) comparator_2 (.a(A), .b(B), .lt(SLtu1));  // open: gt, eq
  Multiplier #(.width(32)) multiplier_1 (.a(A), .b(B), .out(multiplier_1_out), .cout(multiplier_1_cout));  // open: cin
  Multiplicacion multiplicacion_1 (.X(A), .Y(B), .OH(multiplicacion_1_oh), .OL(multiplicacion_1_ol));  // open: in_1
  Divider #(.width(32)) divider_1 (.a(A), .b(B), .out(divider_1_out), .rem(divider_1_rem));  // open: upper
  Division division_1 (.in_2(A), .in_3(B), .DivRem(division_1_divrem), .Div(division_1_div));  // open: in_1
  Multiplexer #(.select(4), .width(32), .enable("false")) multiplexer_1 (
    .in0(Hi), .in1(Hi), .in2(Hi), .in3(Hi), .in4(Hi), .in5(Hi), .in6(Hi), .in7(Hi), .in8(multiplier_1_cout),
    .in9(multiplicacion_1_oh), .in10(divider_1_rem), .in11(division_1_divrem), .in12(Hi), .in13(Hi),
    .in14(Hi), .in15(Hi), .out(multiplexer_1_out), .sel(Input));
  Multiplexer #(.select(4), .width(32), .enable("false")) multiplexer_2 (
    .in0(adder_1_out), .in1(subtractor_1_out), .in2(and_1_out), .in3(or_1_out), .in4(nor_1_out),
    .in5(xor_1_out), .in6({{31{1'b0}}, SLt1}), .in7({{31{1'b0}}, SLtu1}), .in8(multiplier_1_out),
    .in9(multiplicacion_1_ol), .in10(divider_1_out), .in11(division_1_div), .out(multiplexer_2_out),
    .sel(Input));  // open: in12, in13, in14, in15
  Demultiplexer #(.width(32), .enable("false")) demultiplexer_1 (
    .out0(out_7), .out1(demultiplexer_1_out1), .in(multiplexer_2_out), .sel(Input[3]));
  Register #(.width(32)) register_1 (.D(multiplexer_1_out), .en(write), .Q(Hi), .clk(reloj), .clr(reset));
  and and_2 (and_2_out, Input[3], write);
  Register #(.width(32)) register_2 (.D(demultiplexer_1_out1), .en(and_2_out), .Q(Lo), .clk(reloj), .clr(reset));

  // Other names for the same wires on the sheet: SLt32[0] = SLt1; SLtu32[0] = SLtu1
endmodule

module Register_File (
  input  in_1,
  input  [4:0] in_2,
  input  [4:0] in_3,
  input  [4:0] in_4,
  input  [31:0] in_5,
  input  in_6,
  input  in_7,
  input  in_8,
  input  in_9,
  input  in_10,
  output [31:0] out_11,
  output [31:0] A,
  output [31:0] B
);

  wire and_1_out, L1, L2, L3, L4, L5, L6, L7, L8, L9, L10, L11, L12, L13, L14, L15, L16, L17, L18, L19, L20,
       L21, L22, L23, L24, L25, L26, L27, L28, L29, L30, L31, L32, or_1_out;
  wire [31:0] adder_1_out, multiplexer_1_out, multiplexer_2_out, multiplexer_3_out, Q0, Q1, Q2, Q3, Q4, Q5,
       Q6, Q7, Q8, Q9, Q10, Q11, Q12, Q13, Q14, Q15, Q16, Q17, Q18, Q19, Q20, Q21, Q22, Q23, Q24, Q25, Q26,
       Q27, Q28, Q29, Q30, subtractor_1_out;

  Subtractor #(.width(32)) subtractor_1 (.a(out_11), .b(32'h4), .out(subtractor_1_out));  // open: bin, bout
  Adder #(.width(32)) adder_1 (.a(out_11), .b(32'h4), .out(adder_1_out));  // open: cin, cout
  Demultiplexer #(.select(5), .enable("false")) demultiplexer_1 (
    .out0(L1), .out1(L2), .out2(L3), .out3(L4), .out4(L5), .out5(L6), .out6(L7), .out7(L8), .out8(L9),
    .out9(L10), .out10(L11), .out11(L12), .out12(L13), .out13(L14), .out14(L15), .out15(L16), .out16(L17),
    .out17(L18), .out18(L19), .out19(L20), .out20(L21), .out21(L22), .out22(L23), .out23(L24), .out24(L25),
    .out25(L26), .out26(L27), .out27(L28), .out28(L29), .out29(L30), .out30(L31), .out31(L32), .in(in_6),
    .sel(in_4));
  Multiplexer #(.width(32), .enable("false")) multiplexer_1 (
    .in0(subtractor_1_out), .in1(adder_1_out), .out(multiplexer_1_out), .sel(in_7));
  Multiplexer #(.width(32), .enable("false")) multiplexer_2 (
    .in0(multiplexer_1_out), .in1({32{1'b1}}), .out(multiplexer_2_out), .sel(in_9));
  Multiplexer #(.width(32), .enable("false")) multiplexer_3 (
    .in0(multiplexer_2_out), .in1(in_5), .out(multiplexer_3_out), .sel(L32));
  and and_1 (and_1_out, in_10, in_8);
  or or_1 (or_1_out, L32, and_1_out, in_9);
  Register #(.width(32)) register_1 (.D({32{1'b0}}), .en(L1), .Q(Q0), .clk(in_1), .clr(in_9));
  Register #(.width(32)) register_2 (.D(in_5), .en(L2), .Q(Q1), .clk(in_1), .clr(in_9));
  Register #(.width(32)) register_3 (.D(in_5), .en(L3), .Q(Q2), .clk(in_1), .clr(in_9));
  Register #(.width(32)) register_4 (.D(in_5), .en(L4), .Q(Q3), .clk(in_1), .clr(in_9));
  Register #(.width(32)) register_5 (.D(in_5), .en(L5), .Q(Q4), .clk(in_1), .clr(in_9));
  Register #(.width(32)) register_6 (.D(in_5), .en(L6), .Q(Q5), .clk(in_1), .clr(in_9));
  Register #(.width(32)) register_7 (.D(in_5), .en(L7), .Q(Q6), .clk(in_1), .clr(in_9));
  Register #(.width(32)) register_8 (.D(in_5), .en(L8), .Q(Q7), .clk(in_1), .clr(in_9));
  Register #(.width(32)) register_9 (.D(in_5), .en(L9), .Q(Q8), .clk(in_1), .clr(in_9));
  Register #(.width(32)) register_10 (.D(in_5), .en(L10), .Q(Q9), .clk(in_1), .clr(in_9));
  Register #(.width(32)) register_11 (.D(in_5), .en(L11), .Q(Q10), .clk(in_1), .clr(in_9));
  Register #(.width(32)) register_12 (.D(in_5), .en(L12), .Q(Q11), .clk(in_1), .clr(in_9));
  Register #(.width(32)) register_13 (.D(in_5), .en(L13), .Q(Q12), .clk(in_1), .clr(in_9));
  Register #(.width(32)) register_14 (.D(in_5), .en(L14), .Q(Q13), .clk(in_1), .clr(in_9));
  Register #(.width(32)) register_15 (.D(in_5), .en(L15), .Q(Q14), .clk(in_1), .clr(in_9));
  Register #(.width(32)) register_16 (.D(in_5), .en(L16), .Q(Q15), .clk(in_1), .clr(in_9));
  Register #(.width(32)) register_17 (.D(in_5), .en(L17), .Q(Q16), .clk(in_1), .clr(in_9));
  Register #(.width(32)) register_18 (.D(in_5), .en(L18), .Q(Q17), .clk(in_1), .clr(in_9));
  Register #(.width(32)) register_19 (.D(in_5), .en(L19), .Q(Q18), .clk(in_1), .clr(in_9));
  Register #(.width(32)) register_20 (.D(in_5), .en(L20), .Q(Q19), .clk(in_1), .clr(in_9));
  Register #(.width(32)) register_21 (.D(in_5), .en(L21), .Q(Q20), .clk(in_1), .clr(in_9));
  Register #(.width(32)) register_22 (.D(in_5), .en(L22), .Q(Q21), .clk(in_1), .clr(in_9));
  Register #(.width(32)) register_23 (.D(in_5), .en(L23), .Q(Q22), .clk(in_1), .clr(in_9));
  Register #(.width(32)) register_24 (.D(in_5), .en(L24), .Q(Q23), .clk(in_1), .clr(in_9));
  Register #(.width(32)) register_25 (.D(in_5), .en(L25), .Q(Q24), .clk(in_1), .clr(in_9));
  Register #(.width(32)) register_26 (.D(in_5), .en(L26), .Q(Q25), .clk(in_1), .clr(in_9));
  Register #(.width(32)) register_27 (.D(in_5), .en(L27), .Q(Q26), .clk(in_1), .clr(in_9));
  Register #(.width(32)) register_28 (.D(in_5), .en(L28), .Q(Q27), .clk(in_1), .clr(in_9));
  Register #(.width(32)) register_29 (.D(in_5), .en(L29), .Q(Q28), .clk(in_1), .clr(in_9));
  Register #(.width(32)) register_30 (.D(in_5), .en(L30), .Q(Q29), .clk(in_1), .clr(in_9));
  Register #(.width(32)) register_31 (.D(in_5), .en(L31), .Q(Q30), .clk(in_1), .clr(in_9));
  Register #(.width(32)) register_32 (.D(multiplexer_3_out), .en(or_1_out), .Q(out_11), .clk(in_1), .clr(in_9));
  Multiplexer #(.select(5), .width(32), .enable("false")) multiplexer_4 (
    .in0(Q0), .in1(Q1), .in2(Q2), .in3(Q3), .in4(Q4), .in5(Q5), .in6(Q6), .in7(Q7), .in8(Q8), .in9(Q9),
    .in10(Q10), .in11(Q11), .in12(Q12), .in13(Q13), .in14(Q14), .in15(Q15), .in16(Q16), .in17(Q17),
    .in18(Q18), .in19(Q19), .in20(Q20), .in21(Q21), .in22(Q22), .in23(Q23), .in24(Q24), .in25(Q25),
    .in26(Q26), .in27(Q27), .in28(Q28), .in29(Q29), .in30(Q30), .in31(out_11), .out(A), .sel(in_2));
  Multiplexer #(.select(5), .width(32), .enable("false")) multiplexer_5 (
    .in0(Q0), .in1(Q1), .in2(Q2), .in3(Q3), .in4(Q4), .in5(Q5), .in6(Q6), .in7(Q7), .in8(Q8), .in9(Q9),
    .in10(Q10), .in11(Q11), .in12(Q12), .in13(Q13), .in14(Q14), .in15(Q15), .in16(Q16), .in17(Q17),
    .in18(Q18), .in19(Q19), .in20(Q20), .in21(Q21), .in22(Q22), .in23(Q23), .in24(Q24), .in25(Q25),
    .in26(Q26), .in27(Q27), .in28(Q28), .in29(Q29), .in30(Q30), .in31(out_11), .out(B), .sel(in_3));

  // Other names for the same wires on the sheet: Data[31:0] = in_5; null_write = in_6; PC_en = in_10; push_pop = in_7;
  //   Q31[31:0] = out_11; R = in_1; reset = in_9; Selector_1[4:0] = in_2; Selector_2[4:0] = in_3;
  //   Selector_3[4:0] = in_4; SP_en = in_8
endmodule

module Instruction_Decoder (
  input  [31:0] in_1,
  output [2:0] Branch,
  output out_3,
  output [3:0] Aritmetic,
  output out_5,
  output out_6,
  output out_7,
  output out_8,
  output [4:0] out_9,
  output [4:0] out_10,
  output [4:0] out_11,
  output [25:0] out_12,
  output out_13,
  output out_14,
  output [15:0] out_15,
  output out_16,
  output out_17,
  output [1:0] Inmediate,
  output [2:0] Output
);

  wire _000000, _111111, Add, Addi, ALUIns, And, Andi, Beq, Bgtz, Blez, Bltz, Bne, Bqe, comparator_2_eq,
       comparator_3_eq, comparator_4_eq, comparator_5_eq, comparator_6_eq, comparator_7_eq, comparator_8_eq,
       comparator_9_eq, comparator_10_eq, comparator_11_eq, comparator_12_eq, comparator_13_eq,
       comparator_14_eq, comparator_15_eq, comparator_16_eq, comparator_17_eq, comparator_19_eq,
       comparator_20_eq, comparator_21_eq, comparator_22_eq, comparator_23_eq, comparator_24_eq,
       comparator_25_eq, comparator_26_eq, Div, Divu, Halt, J, Jr, Mult, Mulu, Nop, Nor, Or, or_1_out,
       or_2_out, or_3_out, or_4_out, or_5_out, or_6_out, or_7_out, or_8_out, or_9_out, or_10_out, or_13_out,
       Ori, Slt, Slti, Sltiu, Sltu, Sub, Xor, Xori;

  Comparator #(.width(6)) comparator_1 (.a(in_1[31:26]), .b({6{1'b0}}), .eq(_000000));  // open: gt, lt
  and and_1 (Nop, _000000, comparator_2_eq);
  Comparator #(.width(6)) comparator_2 (.a(in_1[5:0]), .b({6{1'b0}}), .eq(comparator_2_eq));  // open: gt, lt
  and and_2 (Add, _000000, comparator_3_eq);
  Comparator #(.width(6)) comparator_3 (.a(in_1[5:0]), .b(6'b100000), .eq(comparator_3_eq));  // open: gt, lt
  and and_3 (Sub, _000000, comparator_4_eq);
  Comparator #(.width(6)) comparator_4 (.a(in_1[5:0]), .b(6'b100010), .eq(comparator_4_eq));  // open: gt, lt
  and and_4 (Mult, _000000, comparator_5_eq);
  Comparator #(.width(6)) comparator_5 (.a(in_1[5:0]), .b(6'b011000), .eq(comparator_5_eq));  // open: gt, lt
  and and_5 (Mulu, _000000, comparator_6_eq);
  Comparator #(.width(6)) comparator_6 (.a(in_1[5:0]), .b(6'b011001), .eq(comparator_6_eq));  // open: gt, lt
  and and_6 (Div, _000000, comparator_7_eq);
  Comparator #(.width(6)) comparator_7 (.a(in_1[5:0]), .b(6'b011010), .eq(comparator_7_eq));  // open: gt, lt
  and and_7 (Divu, _000000, comparator_8_eq);
  Comparator #(.width(6)) comparator_8 (.a(in_1[5:0]), .b(6'b011011), .eq(comparator_8_eq));  // open: gt, lt
  and and_8 (Slt, _000000, comparator_9_eq);
  Comparator #(.width(6)) comparator_9 (.a(in_1[5:0]), .b(6'b101010), .eq(comparator_9_eq));  // open: gt, lt
  and and_9 (Sltu, _000000, comparator_10_eq);
  Comparator #(.width(6)) comparator_10 (.a(in_1[5:0]), .b(6'b101011), .eq(comparator_10_eq));  // open: gt, lt
  and and_10 (And, _000000, comparator_11_eq);
  Comparator #(.width(6)) comparator_11 (.a(in_1[5:0]), .b(6'b100100), .eq(comparator_11_eq));  // open: gt, lt
  and and_11 (Or, _000000, comparator_12_eq);
  Comparator #(.width(6)) comparator_12 (.a(in_1[5:0]), .b(6'b100101), .eq(comparator_12_eq));  // open: gt, lt
  and and_12 (Nor, _000000, comparator_13_eq);
  Comparator #(.width(6)) comparator_13 (.a(in_1[5:0]), .b(6'b100111), .eq(comparator_13_eq));  // open: gt, lt
  and and_13 (Xor, _000000, comparator_14_eq);
  Comparator #(.width(6)) comparator_14 (.a(in_1[5:0]), .b(6'b101000), .eq(comparator_14_eq));  // open: gt, lt
  and and_14 (Jr, _000000, comparator_15_eq);
  Comparator #(.width(6)) comparator_15 (.a(in_1[5:0]), .b(6'b001000), .eq(comparator_15_eq));  // open: gt, lt
  and and_15 (out_7, _000000, comparator_16_eq);
  Comparator #(.width(6)) comparator_16 (.a(in_1[5:0]), .b(6'b010000), .eq(comparator_16_eq));  // open: gt, lt
  and and_16 (out_8, _000000, comparator_17_eq);
  Comparator #(.width(6)) comparator_17 (.a(in_1[5:0]), .b(6'b010010), .eq(comparator_17_eq));  // open: gt, lt
  Comparator #(.width(6)) comparator_18 (.a(in_1[31:26]), .b({6{1'b1}}), .eq(_111111));  // open: gt, lt
  Comparator #(.width(6)) comparator_19 (.a(in_1[5:0]), .b({6{1'b1}}), .eq(comparator_19_eq));  // open: gt, lt
  Comparator #(.width(6)) comparator_20 (.a(in_1[5:0]), .b(6'b000001), .eq(comparator_20_eq));  // open: gt, lt
  Comparator #(.width(6)) comparator_21 (.a(in_1[5:0]), .b(6'b000010), .eq(comparator_21_eq));  // open: gt, lt
  Comparator #(.width(6)) comparator_22 (.a(in_1[5:0]), .b(6'b000100), .eq(comparator_22_eq));  // open: gt, lt
  and and_17 (Halt, _111111, comparator_19_eq);
  and and_18 (out_5, _111111, comparator_20_eq);
  and and_19 (out_6, _111111, comparator_21_eq);
  and and_20 (out_3, _111111, comparator_22_eq);
  Comparator #(.width(6)) comparator_23 (.a(in_1[31:26]), .b(6'b111000), .eq(comparator_23_eq));  // open: gt, lt
  Comparator #(.width(6)) comparator_24 (.a(in_1[5:0]), .b({6{1'b0}}), .eq(comparator_24_eq));  // open: gt, lt
  Comparator #(.width(6)) comparator_25 (.a(in_1[31:26]), .b(6'b111000), .eq(comparator_25_eq));  // open: gt, lt
  Comparator #(.width(6)) comparator_26 (.a(in_1[5:0]), .b(6'b000001), .eq(comparator_26_eq));  // open: gt, lt
  or or_1 (or_1_out, And, Andi);
  or or_2 (or_2_out, Or, Ori);
  or or_3 (or_3_out, Xor, Xori);
  or or_4 (or_4_out, Slt, Slti);
  or or_5 (or_5_out, Sltu, Sltiu);
  and and_21 (out_16, comparator_23_eq, comparator_24_eq);
  and and_22 (out_17, comparator_25_eq, comparator_26_eq);
  or or_6 (or_6_out, out_13, Addi, Add, out_14);
  Priority_Encoder #(.select(4)) priority_encoder_1 (
    .in0(or_6_out), .in1(Sub), .in2(or_1_out), .in3(or_2_out), .in4(Nor), .in5(or_3_out), .in6(or_4_out),
    .in7(or_5_out), .in8(Mult), .in9(Mulu), .in10(Div), .in11(Divu), .out(Aritmetic), .gs(ALUIns));  // open: in12, in13, in14, in15, en_out, en_in
  Comparator #(.width(6)) comparator_27 (.a(in_1[31:26]), .b(6'b100011), .eq(out_13));  // open: gt, lt
  Comparator #(.width(6)) comparator_28 (.a(in_1[31:26]), .b(6'b001000), .eq(Addi));  // open: gt, lt
  Comparator #(.width(6)) comparator_29 (.a(in_1[31:26]), .b(6'b001010), .eq(Slti));  // open: gt, lt
  Comparator #(.width(6)) comparator_30 (.a(in_1[31:26]), .b(6'b001011), .eq(Sltiu));  // open: gt, lt
  Comparator #(.width(6)) comparator_31 (.a(in_1[31:26]), .b(6'b001100), .eq(Andi));  // open: gt, lt
  Comparator #(.width(6)) comparator_32 (.a(in_1[31:26]), .b(6'b001101), .eq(Ori));  // open: gt, lt
  Comparator #(.width(6)) comparator_33 (.a(in_1[31:26]), .b(6'b001110), .eq(Xori));  // open: gt, lt
  Comparator #(.width(6)) comparator_34 (.a(in_1[31:26]), .b(6'b101011), .eq(out_14));  // open: gt, lt
  Comparator #(.width(6)) comparator_35 (.a(in_1[31:26]), .b(6'b000100), .eq(Beq));  // open: gt, lt
  Comparator #(.width(6)) comparator_36 (.a(in_1[31:26]), .b(6'b000101), .eq(Bne));  // open: gt, lt
  Comparator #(.width(6)) comparator_37 (.a(in_1[31:26]), .b(6'b000110), .eq(Blez));  // open: gt, lt
  Comparator #(.width(6)) comparator_38 (.a(in_1[31:26]), .b(6'b000111), .eq(Bgtz));  // open: gt, lt
  Comparator #(.width(6)) comparator_39 (.a(in_1[31:26]), .b(6'b000001), .eq(Bltz));  // open: gt, lt
  Comparator #(.width(6)) comparator_40 (.a(in_1[31:26]), .b(6'b000010), .eq(J));  // open: gt, lt
  Priority_Encoder priority_encoder_2 (
    .in0(1'b1), .in1(Beq), .in2(Bne), .in3(Blez), .in4(Bgtz), .in5(Bltz), .in6(J), .in7(Jr), .out(Branch));  // open: en_in, gs, en_out
  or or_7 (or_7_out, out_13, Addi, out_14);
  or or_8 (or_8_out, out_13, out_16);
  or or_9 (or_9_out, out_6, out_7, out_8, out_3, out_5);
  or or_10 (or_10_out, out_14, out_17);
  or or_11 (Inmediate[0], or_7_out, Slti, Sltiu);
  or or_12 (Inmediate[1], Andi, Ori, Xori);
  or or_13 (or_13_out, Bgtz, Bqe, Bne, Blez, Bltz, Jr, J, Nop);
  Priority_Encoder priority_encoder_3 (
    .in0(Halt), .in1(ALUIns), .in3(or_8_out), .in4(or_9_out), .in6(or_10_out), .in7(or_13_out), .out(Output));  // open: in2, in5, en_in, gs, en_out

  assign out_9 = in_1[25:21];
  assign out_10 = in_1[20:16];
  assign out_11 = in_1[15:11];
  assign out_12 = in_1[25:0];
  assign out_15 = in_1[15:0];

  // Other names for the same wires on the sheet: Const[15:0] = in_1[15:0]; Dest[25:0] = in_1[25:0];
  //   FC[5:0] = in_1[5:0]; RD[4:0] = in_1[15:11]; RT[4:0] = in_1[20:16]; RS[4:0] = in_1[25:21]; Kbd = out_3;
  //   Lw = out_13; Mfhi = out_7; Mflo = out_8; OP[5:0] = in_1[31:26]; Pop = out_16; Push = out_17; Rnd = out_6;
  //   Sw = out_14; Tty = out_5
endmodule

module Data_Path (
  input  in_1,
  input  in_2,
  input  in_3,
  input  [31:0] Data_RAM,
  input  Enable,
  input  in_6,
  input  [6:0] KBD,
  output [31:0] address,
  output Tty,
  output [2:0] out_10,
  output [31:0] Output,
  output [6:0] Tty_2
);

  wire comparator_1_eq, comparator_2_eq, kbd_t, lw, mfhi, mflo, not_1_out, not_2_out, or_1_out, or_2_out,
       pop, push, Rnd, sw;
  wire [1:0] Inmediate;
  wire [2:0] Instrucciones_branch, priority_encoder_1_out;
  wire [3:0] operation;
  wire [4:0] multiplexer_2_out, RD, RS, RT;
  wire [15:0] Const;
  wire [25:0] Dest;
  wire [31:0] Almacenar_Inst_q, B, bit_extender_1_out, branch_control_1_out, Hi, Lo, multiplexer_3_out,
       multiplexer_4_out, PC, random_1_out, Resultado, SP;
  wire [31:7] A;
  wire [31:31] Operando;

  Multiplexer #(.width(32), .enable("false")) multiplexer_1 (.in0({A, Tty_2}), .in1(B), .out(Output), .sel(sw));
  Register #(.width(32)) Almacenar_Inst (.D(Data_RAM), .en(Enable), .Q(Almacenar_Inst_q), .clk(in_2), .clr(in_1));
  Instruction_Decoder instruction_decoder_1 (
    .in_1(Almacenar_Inst_q), .out_13(lw), .out_3(kbd_t), .out_9(RS), .out_14(sw), .out_10(RT), .out_5(Tty),
    .out_11(RD), .out_6(Rnd), .out_12(Dest), .out_16(pop), .out_17(push), .out_15(Const),
    .Aritmetic(operation), .Inmediate(Inmediate), .Branch(Instrucciones_branch), .Output(out_10),
    .out_7(mfhi), .out_8(mflo));
  assign bit_extender_1_out = {{25{1'b0}}, KBD};  // Bit_Extender bit_extender_1
  or or_1 (or_1_out, lw, pop);
  Random #(.width(32)) random_1 (.clk(in_2), .next(Rnd), .out(random_1_out));  // open: clr
  Memory_Address memory_address_1 (
    .in_1(PC), .in_2(Resultado), .in_3(SP), .in_4(lw), .in_5(sw), .in_6(pop), .in_7(push), .in_8(in_3),
    .OUT(address));
  Priority_Encoder priority_encoder_1 (
    .in0(1'b1), .in1(Rnd), .in2(or_1_out), .in3(mflo), .in4(mfhi), .in5(kbd_t), .out(priority_encoder_1_out));  // open: in6, in7, en_in, gs, en_out
  Multiplexer #(.width(5), .enable("false")) multiplexer_2 (
    .in0(RD), .in1(RT), .out(multiplexer_2_out), .sel(not_1_out));
  not not_1 (not_1_out, comparator_1_eq);
  Comparator #(.width(2)) comparator_1 (.a(Inmediate), .b(2'b00), .eq(comparator_1_eq));  // open: gt, lt
  Multiplexer #(.select(3), .width(32), .enable("false")) multiplexer_3 (
    .in0(Resultado), .in1(random_1_out), .in2(Data_RAM), .in3(Lo), .in4(Hi), .in5(bit_extender_1_out),
    .out(multiplexer_3_out), .sel(priority_encoder_1_out));  // open: in6, in7
  or or_2 (or_2_out, pop, push);
  Register #(.width(32)) Program_Counter (.D(branch_control_1_out), .en(in_3), .Q(PC), .clk(in_2));  // open: clr
  Register_File register_file_1 (
    .in_1(in_2), .in_2(RS), .in_3(RT), .in_4(multiplexer_2_out), .in_5(multiplexer_3_out), .in_6(in_6),
    .A({A, Tty_2}), .B(B), .in_7(pop), .in_8(or_2_out), .in_9(in_1), .in_10(in_3), .out_11(SP));
  // Probe on {A, Tty_2}
  // Probe on B
  and and_1 (Operando[31], ~Inmediate[1], Const[15]);  // AND_Gate
  Multiplexer #(.width(32), .enable("false")) multiplexer_4 (
    .in0(B), .in1({{16{Operando[31]}}, Const}), .out(multiplexer_4_out), .sel(not_2_out));
  not not_2 (not_2_out, comparator_2_eq);
  Comparator #(.width(2)) comparator_2 (.a(Inmediate), .b(2'b00), .eq(comparator_2_eq));  // open: gt, lt
  Branch_Control branch_control_1 (
    .in_1(Dest), .in_2({A, Tty_2}), .in_3(B), .in_4(PC), .OUT(branch_control_1_out), .in_5(Const),
    .in_6(Instrucciones_branch));
  ALU alu_1 (
    .A({A, Tty_2}), .B(multiplexer_4_out), .Input(operation), .out_7(Resultado), .Hi(Hi), .Lo(Lo),
    .reset(in_1), .reloj(in_2), .write(in_6));
  // Probe on Resultado

  // Other names for the same wires on the sheet: A[6:0] = Tty_2; Operando[30:0] = {{15{Operando[31]}}, Const};
  //   data[31:0] = Data_RAM; PC_Enable = in_3; R = in_2; Reset = in_1; wirte = in_6
endmodule

module Division (
  input  in_1,
  input  [31:0] in_2,
  input  [31:0] in_3,
  output [31:0] DivRem,
  output [31:0] Div
);

  wire shr_1_p3, shr_2_p3, SignX, SignY, xor_1_out;
  wire [31:0] adder_1_out, Div_t, multiplexer_4_out, negator_1_out, negator_2_out, negator_3_out, Rem,
       subtractor_1_out, X1, Y1;

  // SHR shr_1: pin names not known; wires that end beside it: in_2, 1'b0, shr_1_p3
  // SHR shr_2: pin names not known; wires that end beside it: in_3, 1'b0, shr_2_p3
  Negator #(.width(32)) negator_1 (.in(in_2), .out(negator_1_out));
  Negator #(.width(32)) negator_2 (.in(in_3), .out(negator_2_out));
  and and_1 (SignX, in_1, shr_1_p3);
  and and_2 (SignY, in_1, shr_2_p3);
  Multiplexer #(.width(32)) multiplexer_1 (.in0(in_2), .in1(negator_1_out), .out(X1), .sel(SignX));  // open: en
  Multiplexer #(.width(32)) multiplexer_2 (.in0(in_3), .in1(negator_2_out), .out(Y1), .sel(SignY));  // open: en
  Subtractor #(.width(32)) subtractor_1 (.a(Y1), .b(Rem), .out(subtractor_1_out));  // open: bin, bout
  Divider #(.width(32)) divider_1 (.a(X1), .b(Y1), .out(Div_t), .rem(Rem));  // open: upper
  Multiplexer #(.width(32)) multiplexer_3 (.in0(Rem), .in1(subtractor_1_out), .out(DivRem), .sel(SignX));  // open: en
  Adder #(.width(32)) adder_1 (.a(Div_t), .b(32'h1), .out(adder_1_out));  // open: cin, cout
  Multiplexer #(.width(32)) multiplexer_4 (
    .in0(Div_t), .in1(adder_1_out), .out(multiplexer_4_out), .sel(SignX));  // open: en
  Negator #(.width(32)) negator_3 (.in(multiplexer_4_out), .out(negator_3_out));
  Multiplexer #(.width(32)) multiplexer_5 (
    .in0(multiplexer_4_out), .in1(negator_3_out), .out(Div), .sel(xor_1_out));  // open: en
  xor xor_1 (xor_1_out, SignY, SignX);

  // Other names for the same wires on the sheet: OH[31:0] = DivRem; OL[31:0] = Div; Sign = in_1; X[31:0] = in_2;
  //   Y[31:0] = in_3
endmodule

module SHL (
  input  [31:0] X,
  input  in_2,
  output out_3,
  output [31:0] X_2
);


  assign out_3 = X[0];
  assign X_2 = {in_2, X[31:1]};
endmodule

module SHR (
  input  [31:0] X,
  input  in_2,
  output out_3,
  output [31:0] X_2
);


  assign out_3 = X[31];
  assign X_2 = {X[30:0], in_2};
endmodule

module Multiplicacion (
  input  in_1,
  input  [31:0] X,
  input  [31:0] Y,
  output [31:0] OH,
  output [31:0] OL
);

  wire and_1_out, Overflow, Overflow1, shr_2_out_3, shr_4_out_3, SigX, SigY;
  wire [31:0] NA, NAA, NB, NBB, OH1, OH2, OL1, OL2, RH, RH1, RL, RL1, shl_1_x_2, shl_2_x_2, shr_1_x_2,
       shr_6_x_2, shr_7_x_2, subtractor_1_out, SumX, SumY;

  and and_1 (and_1_out, SigX, SigY);
  SHR shr_1 (.X({32{1'b0}}), .in_2(and_1_out), .X_2(shr_1_x_2));  // open: out_3
  Subtractor #(.width(32)) subtractor_1 (.a(X), .b(shr_1_x_2), .out(subtractor_1_out));  // open: bin, bout
  SHL shl_1 (.X(X), .in_2(1'b0), .out_3(SigX), .X_2(shl_1_x_2));
  SHL shl_2 (.X(Y), .in_2(1'b0), .out_3(SigY), .X_2(shl_2_x_2));
  Multiplexer #(.width(32)) multiplexer_1 (
    .in0({32{1'b0}}), .in1(subtractor_1_out), .out(SumX), .sel(SigY));  // open: en
  Multiplexer #(.width(32)) multiplexer_2 (.in0({32{1'b0}}), .in1(Y), .out(SumY), .sel(SigX));  // open: en
  Multiplier #(.width(32)) multiplier_1 (.a(X), .b(Y), .out(OL1), .cout(OH1));  // open: cin
  Multiplier #(.width(32)) multiplier_2 (.a(shl_1_x_2), .b(shl_2_x_2), .out(OL2), .cout(OH2));  // open: cin
  SHR shr_2 (.X(OL2), .in_2(1'b0), .out_3(shr_2_out_3), .X_2(NA));
  SHR shr_3 (.X(OH2), .in_2(shr_2_out_3), .X_2(NB));  // open: out_3
  SHR shr_4 (.X(NA), .in_2(1'b0), .out_3(shr_4_out_3), .X_2(NAA));
  SHR shr_5 (.X(NB), .in_2(shr_4_out_3), .X_2(NBB));  // open: out_3
  Adder #(.width(32)) adder_1 (.a(NAA), .b(SumX), .out(RL), .cout(Overflow));  // open: cin
  Adder #(.width(32)) adder_2 (.a(RL), .b(SumY), .out(RL1), .cout(Overflow1));  // open: cin
  SHR shr_6 (.X({32{1'b0}}), .in_2(Overflow), .X_2(shr_6_x_2));  // open: out_3
  SHR shr_7 (.X({32{1'b0}}), .in_2(Overflow1), .X_2(shr_7_x_2));  // open: out_3
  Multiplexer #(.width(32)) multiplexer_3 (.in0(RL1), .in1(OL1), .out(OL), .sel(in_1));  // open: en
  Multiplexer #(.width(32)) multiplexer_4 (.in0(RH1), .in1(OH1), .out(OH), .sel(in_1));  // open: en
  Adder #(.width(32)) adder_3 (.a(NBB), .b(shr_6_x_2), .out(RH));  // open: cin, cout
  Adder #(.width(32)) adder_4 (.a(RH), .b(shr_7_x_2), .out(RH1));  // open: cin, cout

  // Other names for the same wires on the sheet: Sign = in_1
endmodule

module Branch_Control (
  input  [25:0] in_1,
  input  [31:0] in_2,
  input  [31:0] in_3,
  input  [31:0] in_4,
  input  [15:0] in_5,
  input  [2:0] in_6,
  output [31:0] OUT
);

  wire and_1_out, and_2_out, and_3_out, and_4_out, and_5_out, Beq, Bgtz, Blez, Bltz, Bne, comparator_1_eq, J,
       Jr, or_2_out, RS_0, RS__0, RS__RT;
  wire [1:0] or_3_out;
  wire [13:0] bit_extender_1_out;
  wire [31:0] PC_4, PC_4_Const;

  Comparator #(.width(32)) comparator_1 (.a(in_2), .b({32{1'b0}}), .eq(comparator_1_eq), .lt(RS_0));  // open: gt
  Comparator #(.width(32)) comparator_2 (.a(in_2), .b(in_3), .eq(RS__RT));  // open: gt, lt
  and and_1 (and_1_out, Beq, RS__RT);
  and and_2 (and_2_out, ~RS__RT, Bne);  // AND_Gate
  and and_3 (and_3_out, Blez, RS__0);
  and and_4 (and_4_out, ~RS__0, Bgtz);  // AND_Gate
  and and_5 (and_5_out, Bltz, RS_0);
  or or_1 (RS__0, comparator_1_eq, RS_0);
  or or_2 (or_2_out, and_1_out, and_2_out, and_3_out, and_4_out, and_5_out);
  or or_3 (or_3_out[0], or_2_out, Jr);
  or or_4 (or_3_out[1], J, Jr);
  Multiplexer #(.select(2), .width(32)) multiplexer_1 (
    .in0(PC_4), .in1(PC_4_Const), .in2({in_4[31:28], in_1, 2'b00}), .in3(in_2), .out(OUT), .sel(or_3_out));  // open: en
  Adder #(.width(32)) adder_1 (.a(in_4), .b(32'h4), .out(PC_4));  // open: cin, cout
  assign bit_extender_1_out = {{13{in_5[15]}}, in_5[15]};  // Bit_Extender bit_extender_1
  Adder #(.width(32)) adder_2 (.a(PC_4), .b({bit_extender_1_out, in_5, 2'b00}), .out(PC_4_Const));  // open: cin, cout
  Decoder #(.select(3)) decoder_1 (
    .out1(Beq), .out2(Bne), .out3(Blez), .out4(Bgtz), .out5(Bltz), .out6(J), .out7(Jr), .sel(in_6));  // open: out0, en

  // Other names for the same wires on the sheet: Const[15:0] = in_5; branch_ins[2:0] = in_6; Dest[25:0] = in_1;
  //   Jmp[31:2] = {in_4[31:28], in_1}; PC[31:0] = in_4; RS[31:0] = in_2; RT[31:0] = in_3
endmodule

module Control_Unit (
  input  start,
  input  in_2,
  input  reloj,
  input  in_4,
  input  in_5,
  input  in_6,
  input  [2:0] in_7,
  input  in_8,
  output out_9,
  output out_10,
  output out_11,
  output out_12,
  output out_13,
  output out_14,
  output out_15,
  output out_16,
  output out_17
);

  wire d_ff_1_q, d_ff_2_q, d_ff_5_q, d_ff_6_q, demultiplexer_1_out0, demultiplexer_2_out0,
       demultiplexer_2_out1, demultiplexer_2_out4, demultiplexer_2_out7, demultiplexer_3_out0,
       demultiplexer_3_out1, demultiplexer_4_out0, demultiplexer_4_out1, or_1_out, or_2_out, or_3_out,
       or_4_out, or_5_out;

  or or_1 (or_1_out, out_13, start);
  D_Flip_Flop #(.trigger("falling")) IDLE (
    .clk(reloj), .D(or_1_out), .Q(out_12), .reset(in_2));  // open: Qn, preset, en
  or or_2 (or_2_out, demultiplexer_1_out0, out_12);
  and and_1 (out_15, out_16, in_8);
  D_Flip_Flop #(.trigger("falling")) d_ff_1 (
    .clk(reloj), .D(or_2_out), .Q(d_ff_1_q), .reset(in_2));  // open: Qn, preset, en
  Demultiplexer #(.enable("false")) demultiplexer_1 (
    .out0(demultiplexer_1_out0), .out1(out_14), .in(d_ff_1_q), .sel(in_4));
  D_Flip_Flop #(.trigger("falling")) d_ff_2 (
    .clk(reloj), .D(out_14), .Q(d_ff_2_q), .reset(in_2));  // open: Qn, preset, en
  Demultiplexer #(.select(3), .enable("false")) demultiplexer_2 (
    .out0(demultiplexer_2_out0), .out1(demultiplexer_2_out1), .out3(out_11), .out4(demultiplexer_2_out4),
    .out6(out_10), .out7(demultiplexer_2_out7), .in(d_ff_2_q), .sel(in_7));  // open: out2, out5
  or or_3 (or_3_out, out_17, demultiplexer_2_out0);
  or or_4 (or_4_out, demultiplexer_3_out0, out_11);
  or or_5 (or_5_out, demultiplexer_4_out0, out_10);
  D_Flip_Flop #(.trigger("falling")) d_ff_3 (
    .clk(reloj), .D(or_3_out), .Q(out_17), .reset(in_2));  // open: Qn, preset, en
  D_Flip_Flop #(.trigger("falling")) d_ff_4 (.clk(reloj), .reset(in_2));  // open: D, Q, Qn, preset, en
  D_Flip_Flop #(.trigger("falling")) d_ff_5 (
    .clk(reloj), .D(or_4_out), .Q(d_ff_5_q), .reset(in_2));  // open: Qn, preset, en
  D_Flip_Flop #(.trigger("falling")) d_ff_6 (
    .clk(reloj), .D(or_5_out), .Q(d_ff_6_q), .reset(in_2));  // open: Qn, preset, en
  Demultiplexer #(.enable("false")) demultiplexer_3 (
    .out0(demultiplexer_3_out0), .out1(demultiplexer_3_out1), .in(d_ff_5_q), .sel(in_5));
  Demultiplexer #(.enable("false")) demultiplexer_4 (
    .out0(demultiplexer_4_out0), .out1(demultiplexer_4_out1), .in(d_ff_6_q), .sel(in_6));
  or or_6 (out_9, demultiplexer_2_out1, demultiplexer_3_out1, demultiplexer_2_out4);
  D_Flip_Flop #(.trigger("falling")) d_ff_7 (.clk(reloj), .D(out_9), .Q(out_16), .reset(in_2));  // open: Qn, preset, en
  or or_7 (out_13, out_16, demultiplexer_4_out1, demultiplexer_2_out7);

  // Other names for the same wires on the sheet: Enable_PC = out_13; EnableIns = out_14; End = out_17;
  //   get_Data = out_11; get_ins = out_12; R = reloj; ReadyData = in_5; ReadyIns = in_4; ReadyW = in_6; Reset = in_2;
  //   tipo_Ins[2:0] = in_7; KBD = out_16; Tty = out_16; TtyEnable = out_15; TtyIns = in_8; UseRF = out_9;
  //   Write = out_10

  // Notes on the sheet:
  //   Halt
  //   ALU
  //   ReadRAM
  //   Instrucciones especiales
  //   WriteRAM
  //   Jumps
endmodule

module RAM_interaction (
  input  [31:0] in_1,
  input  [3:0] Read_Time,
  input  in_3,
  input  in_4,
  input  in_5,
  input  in_6,
  input  in_7,
  input  [3:0] Write_Time,
  input  [31:0] RAM_Out_0,
  input  [31:0] RAM_Out_1,
  input  [31:0] RAM_Out_2,
  input  [31:0] RAM_Out_3,
  output [15:0] Address,
  output [3:0] Mask,
  output out_15,
  output out_16,
  output out_17,
  output nRead_Write,
  output Chip_Select,
  output [31:0] RAM_In_0,
  output [31:0] RAM_In_1,
  output [31:0] RAM_In_2,
  output [31:0] RAM_In_3
);

  wire counter_2_ready, counter_3_ready, CSD, CSI, or_1_out, or_2_out, or_3_out, or_6_out, or_7_out, Stop0,
       x, x1, x2;

  or or_1 (or_1_out, in_6, counter_2_ready);
  or or_2 (or_2_out, in_7, counter_3_ready);
  D_Flip_Flop #(.trigger("falling")) d_ff_1 (
    .clk(in_4), .D(in_5), .Q(nRead_Write), .en(or_3_out), .reset(in_3));  // open: Qn, preset
  or or_3 (or_3_out, in_5, Stop0);
  D_Flip_Flop #(.trigger("falling")) d_ff_2 (
    .clk(in_4), .D(in_6), .Q(CSD), .en(or_1_out), .reset(in_3));  // open: Qn, preset
  D_Flip_Flop #(.trigger("falling")) d_ff_3 (
    .clk(in_4), .D(in_7), .Q(CSI), .en(or_2_out), .reset(in_3));  // open: Qn, preset
  Register #(.width(32)) register_1 (.D(RAM_Out_0), .en(x), .Q(RAM_In_0), .clk(in_4), .clr(in_3));
  Register #(.width(32)) register_2 (.D(RAM_Out_1), .en(x), .Q(RAM_In_1), .clk(in_4), .clr(in_3));
  Counter counter_1 (.reset(out_15), .clk(in_4), .start(nRead_Write), .in_4(Write_Time), .Ready(Stop0));
  Counter counter_2 (.reset(out_16), .clk(in_4), .start(CSD), .in_4(Read_Time), .Ready(counter_2_ready));
  Counter counter_3 (.reset(out_17), .clk(in_4), .start(CSI), .in_4(Read_Time), .Ready(counter_3_ready));
  Register #(.width(32)) register_3 (.D(RAM_Out_2), .en(x), .Q(RAM_In_2), .clk(in_4), .clr(in_3));
  Register #(.width(32)) register_4 (.D(RAM_Out_3), .en(x), .Q(RAM_In_3), .clk(in_4), .clr(in_3));
  D_Flip_Flop #(.trigger("falling")) d_ff_4 (.clk(in_4), .D(Stop0), .Q(out_15), .reset(in_3));  // open: Qn, preset, en
  D_Flip_Flop #(.trigger("falling")) d_ff_5 (
    .clk(in_4), .D(counter_2_ready), .Q(x1), .reset(out_16));  // open: Qn, preset, en
  D_Flip_Flop #(.trigger("falling")) d_ff_6 (
    .clk(in_4), .D(counter_3_ready), .Q(x2), .reset(out_17));  // open: Qn, preset, en
  D_Flip_Flop #(.trigger("falling")) d_ff_7 (.clk(in_4), .D(x1), .Q(out_16));  // open: Qn, preset, en, reset
  D_Flip_Flop #(.trigger("falling")) d_ff_8 (.clk(in_4), .D(x2), .Q(out_17));  // open: Qn, preset, en, reset
  or or_4 (x, x1, x2);
  or or_5 (Chip_Select, nRead_Write, or_6_out, or_7_out);
  Demultiplexer #(.select(2)) demultiplexer_1 (
    .out0(Mask[0]), .out1(Mask[1]), .out2(Mask[2]), .out3(Mask[3]), .in(1'b1), .sel(in_1[3:2]));  // open: en
  or or_6 (or_6_out, CSD, x1);
  or or_7 (or_7_out, CSI, x2);

  assign Address = in_1[19:4];

  // Other names for the same wires on the sheet: Clk = in_4; DPAddress[31:0] = in_1; RAM_A[15:0] = in_1[19:4];
  //   get_Data = in_6; get_ins = in_7; RAM_INPUT_0[31:0] = RAM_In_0; RAM_INPUT_1[31:0] = RAM_In_1;
  //   RAM_INPUT_2[31:0] = RAM_In_2; RAM_INPUT_3[31:0] = RAM_In_3; RAM_MASK[3:0] = Mask;
  //   RAM_OUTPUT_0[31:0] = RAM_Out_0; RAM_OUTPUT_1[31:0] = RAM_Out_1; RAM_OUTPUT_2[31:0] = RAM_Out_2;
  //   RAM_OUTPUT_3[31:0] = RAM_Out_3; ReadyData = out_16; ReadyIns = out_17; ReadyW = out_15; reset = in_3;
  //   RW = nRead_Write; Write = in_5

  // Notes on the sheet:
  //   RAM ADDRESS
  //   DATA FROM RAM
  //   DATA TO RAM
  //   DATA WRITE MASK
  //   RAM TIMING
  //   RAM CONTROL
endmodule

module Counter (
  input  start,
  input  reset,
  input  clk,
  input  [3:0] in_4,
  output Ready
);

  wire [3:0] counter_1_q;

  Counter_part #(.width(4), .max('hf)) counter_1 (
    .count(start), .Q(counter_1_q), .clk(clk), .clr(reset));  // open: load, D, carry
  Comparator #(.width(4)) comparator_1 (.a(in_4), .b(counter_1_q), .eq(Ready));  // open: gt, lt

  // Other names for the same wires on the sheet: Time[3:0] = in_4
endmodule

module Memory_Address (
  input  [31:0] in_1,
  input  [31:0] in_2,
  input  [31:0] in_3,
  input  in_4,
  input  in_5,
  input  in_6,
  input  in_7,
  input  in_8,
  output [31:0] OUT
);

  wire [1:0] or_2_out;
  wire [31:0] multiplexer_1_out, subtractor_1_out;

  Subtractor #(.width(32)) subtractor_1 (.a(in_3), .b(32'h4), .out(subtractor_1_out));  // open: bin, bout
  Multiplexer #(.width(32)) multiplexer_1 (
    .in0(in_3), .in1(subtractor_1_out), .out(multiplexer_1_out), .sel(in_7));  // open: en
  Multiplexer #(.select(2), .width(32)) multiplexer_2 (
    .in0(in_1), .in1(in_2), .in2(multiplexer_1_out), .in3(in_1), .out(OUT), .sel(or_2_out));  // open: en
  or or_1 (or_2_out[1], in_6, in_8, in_7);
  or or_2 (or_2_out[0], in_4, in_8, in_5);

  // Other names for the same wires on the sheet: ALU[31:0] = in_2; isPC = in_8; Lw = in_4; PC[31:0] = in_1;
  //   Pop = in_6; Push = in_7; SP[31:0] = in_3; Sw = in_5
endmodule

module LE (
  input  [31:0] in_1,
  output [31:0] Output
);


  assign Output = {in_1[7:0], in_1[15:8], in_1[23:16], in_1[31:24]};
endmodule
